# Fritzing sketch IncorrectRelays (saved by Fritzing 0.9.3b)

parts:
  U1 = RELAY-SOLIDSTATE [package=relay-s108t02]
  U2 = RELAY-SOLIDSTATE [package=relay-s108t02]
  U3 = RELAY-SOLIDSTATE [package=relay-s108t02]
  U4 = RELAY-SOLIDSTATE [package=relay-s108t02]
  U5 = RELAY-SOLIDSTATE [package=relay-s108t02]
  LED1 = smd LED [color="Red (633nm)" package="0805 [SMD]"]
  LED2 = smd LED [color="Red (633nm)" package="0805 [SMD]"]
  LED3 = smd LED [color="Red (633nm)" package="0805 [SMD]"]
  LED4 = smd LED [color="Red (633nm)" package="0805 [SMD]"]
  LED5 = smd LED [color="Red (633nm)" package="0805 [SMD]"]
  Battery_1 = Battery
  Battery_2 = 4 x AAA Battery Mount

nets:
  N1: U1.T1, U2.T1, U3.T1, U4.T1, U5.T1, Battery_2.+
  N2: U1.T2, LED2.anode
  N3: U1.+, U2.+, U3.+, U4.+, U5.+, Battery_1.+
  N4: U1.-, U2.-, U3.-, U4.-, U5.-, Battery_1.-
  N5: U2.T2, LED3.anode
  N6: U3.T2, LED1.anode
  N7: U4.T2, LED4.anode
  N8: U5.T2, LED5.anode
  N9: LED1.cathode, LED2.cathode, LED3.cathode, LED4.cathode, LED5.cathode, Battery_2.-

custom parts:
  Battery: Your standard 2x 18650 battery pack (7,4 Volts)
